// Logisim project LogKolo NILI - Domaci2.circ as structural Verilog: 2 circuits, main circuit LogKolo NILI (celo)
module LogKolo_NILI__celo (
  input  X1,
  input  X2,
  input  X3,
  input  X4,
  input  X5,
  output Y
);

  wire nor_1_out, nor_2_out, nor_3_out, nor_4_out, nor_5_out, nor_6_out, nor_7_out, nor_8_out, nor_9_out,
       nor_10_out, nor_11_out, nor_12_out, nor_13_out, nor_14_out, nor_15_out;

  nor nor_1 (nor_1_out, X1, X1);
  nor nor_2 (nor_2_out, X2, X2);
  nor nor_3 (nor_3_out, X3, X3);
  nor nor_4 (nor_4_out, X4, X4);
  nor nor_5 (nor_5_out, X5, X5);
  nor nor_6 (nor_6_out, nor_1_out, nor_1_out);
  nor nor_7 (nor_7_out, nor_2_out, nor_2_out);
  nor nor_8 (nor_8_out, nor_4_out, nor_4_out);
  nor nor_9 (nor_9_out, nor_5_out, nor_5_out);
  nor nor_10 (nor_10_out, nor_6_out, nor_7_out);
  nor nor_11 (nor_11_out, nor_8_out, nor_9_out);
  nor nor_12 (nor_12_out, nor_10_out, nor_10_out);
  nor nor_13 (nor_13_out, nor_11_out, nor_11_out);
  nor nor_14 (nor_14_out, nor_12_out, nor_3_out);
  nor nor_15 (nor_15_out, nor_14_out, nor_14_out);
  nor nor_16 (Y, nor_15_out, nor_13_out);

  // Notes on the sheet:
  //   Datum rodjenja : 3.1
  //   3+1=4 | 00100
endmodule

module LogKolo_NILI__skraceno (
  input  X1,
  input  X2,
  input  X3,
  input  X4,
  input  X5,
  output Y
);

  wire nor_1_out, nor_2_out, nor_3_out, nor_4_out, nor_5_out, nor_6_out, nor_7_out;

  nor nor_1 (nor_1_out, X3, X3);
  nor nor_2 (nor_2_out, X1, X2);
  nor nor_3 (nor_3_out, X4, X5);
  nor nor_4 (nor_4_out, nor_2_out, nor_2_out);
  nor nor_5 (nor_5_out, nor_3_out, nor_3_out);
  nor nor_6 (nor_6_out, nor_4_out, nor_1_out);
  nor nor_7 (nor_7_out, nor_6_out, nor_6_out);
  nor nor_8 (Y, nor_7_out, nor_5_out);
endmodule
